// Logisim project AiAlu.circ as structural Verilog
module and8bit (
  input  [7:0] aand,
  input  [7:0] band,
  output [7:0] yand
);

  assign yand = aand & band;  // AND_Gate and_1, 8 bits wide
endmodule

module or8bit (
  input  [7:0] aor,
  input  [7:0] bor,
  output [7:0] yor
);

  assign yor = aor | bor;  // OR_Gate or_1, 8 bits wide
endmodule

module not8bit (
  input  [7:0] in_1,
  input  [7:0] in_2
);

  // NOT_Gate not_1 is placed but not wired
endmodule
